// Logisim project CSE332.2_Project_1911350642_MD. Fatin Habib Nihal.circ as structural Verilog
module _32_bit_register (
  input  [31:0] Write_Data,
  input  [4:0] Read_Resistor_1,
  input  [4:0] Write_Register,
  input  [4:0] Read_Resistor_2,
  input  Write_Enable,
  input  CLK,
  input  CLK_2,
  output [31:0] Read_Data_1,
  output [31:0] Read_Data_2
);

  wire and_1_out, and_2_out, and_3_out, and_4_out, and_5_out, and_6_out, and_7_out, and_8_out, and_9_out,
       and_10_out, and_11_out, and_12_out, and_13_out, and_14_out, and_15_out, and_16_out, and_17_out,
       and_18_out, and_19_out, and_20_out, and_21_out, and_22_out, and_23_out, and_24_out, and_25_out,
       and_26_out, and_27_out, and_28_out, and_29_out, and_30_out, and_31_out, and_32_out, decoder_1_out0,
       decoder_1_out1, decoder_1_out2, decoder_1_out3, decoder_1_out4, decoder_1_out5, decoder_1_out6,
       decoder_1_out7, decoder_1_out8, decoder_1_out9, decoder_1_out10, decoder_1_out11, decoder_1_out12,
       decoder_1_out13, decoder_1_out14, decoder_1_out15, decoder_1_out16, decoder_1_out17, decoder_1_out18,
       decoder_1_out19, decoder_1_out20, decoder_1_out21, decoder_1_out22, decoder_1_out23, decoder_1_out24,
       decoder_1_out25, decoder_1_out26, decoder_1_out27, decoder_1_out28, decoder_1_out29, decoder_1_out30,
       decoder_1_out31;
  wire [31:0] R0_q, R1_q, R2_q, R3_q, R4_q, R5_q, R6_q, R7_q, R8_q, R9_q, R10_q, R11_q, R12_q, R13_q, R14_q,
       R15_q, R16_q, R17_q, R18_q, R19_q, R20_q, R21_q, R22_q, R23_q, R24_q, R25_q, R26_q, R27_q, R28_q,
       R29_q, R30_q, R31_q;

  Decoder #(.select(5), .enable("false")) decoder_1 (
    .out0(decoder_1_out0), .out1(decoder_1_out1), .out2(decoder_1_out2), .out3(decoder_1_out3),
    .out4(decoder_1_out4), .out5(decoder_1_out5), .out6(decoder_1_out6), .out7(decoder_1_out7),
    .out8(decoder_1_out8), .out9(decoder_1_out9), .out10(decoder_1_out10), .out11(decoder_1_out11),
    .out12(decoder_1_out12), .out13(decoder_1_out13), .out14(decoder_1_out14), .out15(decoder_1_out15),
    .out16(decoder_1_out16), .out17(decoder_1_out17), .out18(decoder_1_out18), .out19(decoder_1_out19),
    .out20(decoder_1_out20), .out21(decoder_1_out21), .out22(decoder_1_out22), .out23(decoder_1_out23),
    .out24(decoder_1_out24), .out25(decoder_1_out25), .out26(decoder_1_out26), .out27(decoder_1_out27),
    .out28(decoder_1_out28), .out29(decoder_1_out29), .out30(decoder_1_out30), .out31(decoder_1_out31),
    .sel(Write_Register));
  and and_1 (and_1_out, decoder_1_out0, Write_Enable);
  and and_2 (and_2_out, decoder_1_out1, Write_Enable);
  and and_3 (and_3_out, decoder_1_out2, Write_Enable);
  and and_4 (and_4_out, decoder_1_out3, Write_Enable);
  and and_5 (and_5_out, decoder_1_out4, Write_Enable);
  and and_6 (and_6_out, decoder_1_out5, Write_Enable);
  and and_7 (and_7_out, decoder_1_out6, Write_Enable);
  and and_8 (and_8_out, decoder_1_out7, Write_Enable);
  and and_9 (and_9_out, decoder_1_out8, Write_Enable);
  and and_10 (and_10_out, decoder_1_out9, Write_Enable);
  and and_11 (and_11_out, decoder_1_out10, Write_Enable);
  and and_12 (and_12_out, decoder_1_out11, Write_Enable);
  and and_13 (and_13_out, decoder_1_out12, Write_Enable);
  and and_14 (and_14_out, decoder_1_out13, Write_Enable);
  and and_15 (and_15_out, decoder_1_out14, Write_Enable);
  and and_16 (and_16_out, decoder_1_out15, Write_Enable);
  and and_17 (and_17_out, decoder_1_out16, Write_Enable);
  and and_18 (and_18_out, decoder_1_out17, Write_Enable);
  and and_19 (and_19_out, decoder_1_out18, Write_Enable);
  and and_20 (and_20_out, decoder_1_out19, Write_Enable);
  and and_21 (and_21_out, decoder_1_out20, Write_Enable);
  and and_22 (and_22_out, decoder_1_out21, Write_Enable);
  and and_23 (and_23_out, decoder_1_out22, Write_Enable);
  and and_24 (and_24_out, decoder_1_out23, Write_Enable);
  and and_25 (and_25_out, decoder_1_out24, Write_Enable);
  and and_26 (and_26_out, decoder_1_out25, Write_Enable);
  and and_27 (and_27_out, decoder_1_out26, Write_Enable);
  and and_28 (and_28_out, decoder_1_out27, Write_Enable);
  and and_29 (and_29_out, decoder_1_out28, Write_Enable);
  and and_30 (and_30_out, decoder_1_out29, Write_Enable);
  and and_31 (and_31_out, decoder_1_out30, Write_Enable);
  and and_32 (and_32_out, decoder_1_out31, Write_Enable);
  Register #(.width(32)) R0 (.D(Write_Data), .en(and_1_out), .Q(R0_q), .clk(CLK), .clr(CLK_2));
  Register #(.width(32)) R1 (.D(Write_Data), .en(and_2_out), .Q(R1_q), .clk(CLK), .clr(CLK_2));
  Register #(.width(32)) R2 (.D(Write_Data), .en(and_3_out), .Q(R2_q), .clk(CLK), .clr(CLK_2));
  Register #(.width(32)) R3 (.D(Write_Data), .en(and_4_out), .Q(R3_q), .clk(CLK), .clr(CLK_2));
  Register #(.width(32)) R4 (.D(Write_Data), .en(and_5_out), .Q(R4_q), .clk(CLK), .clr(CLK_2));
  Register #(.width(32)) R5 (.D(Write_Data), .en(and_6_out), .Q(R5_q), .clk(CLK), .clr(CLK_2));
  Register #(.width(32)) R6 (.D(Write_Data), .en(and_7_out), .Q(R6_q), .clk(CLK), .clr(CLK_2));
  Register #(.width(32)) R7 (.D(Write_Data), .en(and_8_out), .Q(R7_q), .clk(CLK), .clr(CLK_2));
  Register #(.width(32)) R8 (.D(Write_Data), .en(and_9_out), .Q(R8_q), .clk(CLK), .clr(CLK_2));
  Register #(.width(32)) R9 (.D(Write_Data), .en(and_10_out), .Q(R9_q), .clk(CLK), .clr(CLK_2));
  Register #(.width(32)) R10 (.D(Write_Data), .en(and_11_out), .Q(R10_q), .clk(CLK), .clr(CLK_2));
  Register #(.width(32)) R11 (.D(Write_Data), .en(and_12_out), .Q(R11_q), .clk(CLK), .clr(CLK_2));
  Register #(.width(32)) R12 (.D(Write_Data), .en(and_13_out), .Q(R12_q), .clk(CLK), .clr(CLK_2));
  Register #(.width(32)) R13 (.D(Write_Data), .en(and_14_out), .Q(R13_q), .clk(CLK), .clr(CLK_2));
  Register #(.width(32)) R14 (.D(Write_Data), .en(and_15_out), .Q(R14_q), .clk(CLK), .clr(CLK_2));
  Register #(.width(32)) R15 (.D(Write_Data), .en(and_16_out), .Q(R15_q), .clk(CLK), .clr(CLK_2));
  Register #(.width(32)) R16 (.D(Write_Data), .en(and_17_out), .Q(R16_q), .clk(CLK), .clr(CLK_2));
  Register #(.width(32)) R17 (.D(Write_Data), .en(and_18_out), .Q(R17_q), .clk(CLK), .clr(CLK_2));
  Register #(.width(32)) R18 (.D(Write_Data), .en(and_19_out), .Q(R18_q), .clk(CLK), .clr(CLK_2));
  Register #(.width(32)) R19 (.D(Write_Data), .en(and_20_out), .Q(R19_q), .clk(CLK), .clr(CLK_2));
  Register #(.width(32)) R20 (.D(Write_Data), .en(and_21_out), .Q(R20_q), .clk(CLK), .clr(CLK_2));
  Register #(.width(32)) R21 (.D(Write_Data), .en(and_22_out), .Q(R21_q), .clk(CLK), .clr(CLK_2));
  Register #(.width(32)) R22 (.D(Write_Data), .en(and_23_out), .Q(R22_q), .clk(CLK), .clr(CLK_2));
  Register #(.width(32)) R23 (.D(Write_Data), .en(and_24_out), .Q(R23_q), .clk(CLK), .clr(CLK_2));
  Register #(.width(32)) R24 (.D(Write_Data), .en(and_25_out), .Q(R24_q), .clk(CLK), .clr(CLK_2));
  Register #(.width(32)) R25 (.D(Write_Data), .en(and_26_out), .Q(R25_q), .clk(CLK), .clr(CLK_2));
  Register #(.width(32)) R26 (.D(Write_Data), .en(and_27_out), .Q(R26_q), .clk(CLK), .clr(CLK_2));
  Register #(.width(32)) R27 (.D(Write_Data), .en(and_28_out), .Q(R27_q), .clk(CLK), .clr(CLK_2));
  Register #(.width(32)) R28 (.D(Write_Data), .en(and_29_out), .Q(R28_q), .clk(CLK), .clr(CLK_2));
  Register #(.width(32)) R29 (.D(Write_Data), .en(and_30_out), .Q(R29_q), .clk(CLK), .clr(CLK_2));
  Register #(.width(32)) R30 (.D(Write_Data), .en(and_31_out), .Q(R30_q), .clk(CLK), .clr(CLK_2));
  Register #(.width(32)) R31 (.D(Write_Data), .en(and_32_out), .Q(R31_q), .clk(CLK), .clr(CLK_2));
  Multiplexer #(.select(5), .width(32), .enable("false")) multiplexer_1 (
    .in0(R0_q), .in1(R1_q), .in2(R2_q), .in3(R3_q), .in4(R4_q), .in5(R5_q), .in6(R6_q), .in7(R7_q),
    .in8(R8_q), .in9(R9_q), .in10(R10_q), .in11(R11_q), .in12(R12_q), .in13(R13_q), .in14(R14_q),
    .in15(R15_q), .in16(R16_q), .in17(R17_q), .in18(R18_q), .in19(R19_q), .in20(R20_q), .in21(R21_q),
    .in22(R22_q), .in23(R23_q), .in24(R24_q), .in25(R25_q), .in26(R26_q), .in27(R27_q), .in28(R28_q),
    .in29(R29_q), .in30(R30_q), .in31(R31_q), .out(Read_Data_1), .sel(Read_Resistor_1));
  Multiplexer #(.select(5), .width(32), .enable("false")) multiplexer_2 (
    .in0(R0_q), .in1(R1_q), .in2(R2_q), .in3(R3_q), .in4(R4_q), .in5(R5_q), .in6(R6_q), .in7(R7_q),
    .in8(R8_q), .in9(R9_q), .in10(R10_q), .in11(R11_q), .in12(R12_q), .in13(R13_q), .in14(R14_q),
    .in15(R15_q), .in16(R16_q), .in17(R17_q), .in18(R18_q), .in19(R19_q), .in20(R20_q), .in21(R21_q),
    .in22(R22_q), .in23(R23_q), .in24(R24_q), .in25(R25_q), .in26(R26_q), .in27(R27_q), .in28(R28_q),
    .in29(R29_q), .in30(R30_q), .in31(R31_q), .out(Read_Data_2), .sel(Read_Resistor_2));
endmodule

module _32_Bit_ALU (
  input  Cin,
  input  [31:0] A,
  input  [31:0] B,
  input  Binv,
  input  [4:0] ALU_op,
  output Cout,
  output [31:0] Result,
  output Zero
);

  wire comparator_1_gt, comparator_1_lt;
  wire [4:0] bit_extender_1_out, bit_extender_2_out;
  wire [31:0] adder_1_out, and_1_out, bit_extender_3_out, bit_extender_4_out, multiplexer_1_out, not_1_out,
       or_1_out, shifter_1_out, shifter_2_out;

  assign not_1_out = ~B;  // NOT_Gate not_1, 32 bits wide
  Bit_Extender #(.in_width(32), .out_width(5)) bit_extender_1 (.in(B), .out(bit_extender_1_out));
  Bit_Extender #(.in_width(32), .out_width(5)) bit_extender_2 (.in(B), .out(bit_extender_2_out));
  Comparator #(.width(32)) comparator_1 (.a(A), .b(B), .gt(comparator_1_gt), .eq(Zero), .lt(comparator_1_lt));
  Multiplexer #(.width(32), .enable("false")) multiplexer_1 (
    .in0(B), .in1(not_1_out), .out(multiplexer_1_out), .sel(Binv));
  Adder #(.width(32)) adder_1 (.a(A), .b(multiplexer_1_out), .out(adder_1_out), .cin(Cin), .cout(Cout));
  assign and_1_out = A & B;  // AND_Gate and_1, 32 bits wide
  assign or_1_out = A | B;  // OR_Gate or_1, 32 bits wide
  Shifter #(.width(32)) shifter_1 (.in(A), .\dist (bit_extender_1_out), .out(shifter_1_out));
  Shifter #(.width(32), .shift("lr")) shifter_2 (.in(A), .\dist (bit_extender_2_out), .out(shifter_2_out));
  assign bit_extender_3_out = {{31{1'b0}}, comparator_1_gt};  // Bit_Extender bit_extender_3
  assign bit_extender_4_out = {{31{1'b0}}, comparator_1_lt};  // Bit_Extender bit_extender_4
  Multiplexer #(.select(5), .width(32), .enable("false")) multiplexer_2 (
    .in0(A), .in1(adder_1_out), .in2(bit_extender_4_out), .in3(and_1_out), .in4(shifter_1_out),
    .in5(or_1_out), .in6(shifter_2_out), .in7(bit_extender_3_out), .out(Result), .sel(ALU_op));  // open: in8, in9, in10, in11, in12, in13, in14, in15, in16, in17, in18, in19, in20, in21, in22, in23, in24, in25, in26, in27, in28, in29, in30, in31
endmodule

module Datapath (
  output [31:0] out_1,
  output [31:0] out_2,
  output [31:0] out_3,
  output [31:0] out_4,
  output [4:0] Rd,
  output [4:0] Rt,
  output [4:0] Rs,
  output out_8,
  output [3:0] opcode,
  output [4:0] Alu_op
);

  wire and_1_out, Clock_out, control_unit_1_alu_src, control_unit_1_b_inv, control_unit_1_branch,
       control_unit_1_c_in, control_unit_1_jump, control_unit_1_ld, control_unit_1_mem2reg,
       control_unit_1_memsel, control_unit_1_regdest, control_unit_1_str, control_unit_1_write_register,
       n32_bit_alu_1_zero, RAM_CLR_out, Reg_CLR_out;
  wire [4:0] multiplexer_1_out;
  wire [15:0] adder_1_out, bit_extender_1_out, register_1_q;
  wire [18:0] bit_extender_5_out, ram_1_data;
  wire [23:0] bit_extender_6_out;
  wire [31:0] adder_2_out, bit_extender_2_out, bit_extender_3_out, bit_extender_4_out, bit_extender_7_out,
       multiplexer_3_out, multiplexer_4_out, n32_bit_register_1_read_data_2;

  Bit_Extender #(.in_width(32)) bit_extender_1 (.in(multiplexer_4_out), .out(bit_extender_1_out));
  Button Reg_CLR (.out(Reg_CLR_out));
  Button Clock (.out(Clock_out));
  Register #(.width(16)) register_1 (.D(bit_extender_1_out), .Q(register_1_q), .clk(Clock_out));  // open: en, clr
  ROM #(.addrWidth(16), .dataWidth(19)) rom_1 (.addr(register_1_q), .data({opcode, Rs, Rt, Rd}));  // open: sel
  Control_Unit control_unit_1 (
    .in_1(opcode), .ALU_Op(Alu_op), .Write_Register(control_unit_1_write_register),
    .B_inv(control_unit_1_b_inv), .C_in(control_unit_1_c_in), .RegDest(control_unit_1_regdest),
    .Alu_Src(control_unit_1_alu_src), .Mem2Reg(control_unit_1_mem2reg), .Str(control_unit_1_str),
    .Ld(control_unit_1_ld), .Branch(control_unit_1_branch), .MemSel(control_unit_1_memsel),
    .Jump(control_unit_1_jump));
  Multiplexer #(.width(5), .enable("false")) multiplexer_1 (
    .in0(Rd), .in1(Rt), .out(multiplexer_1_out), .sel(control_unit_1_regdest));
  _32_bit_register u_32_bit_register_1 (
    .Read_Data_1(out_4), .Read_Data_2(n32_bit_register_1_read_data_2), .Write_Data(out_2),
    .Write_Register(multiplexer_1_out), .Write_Enable(control_unit_1_write_register), .Read_Resistor_1(Rs),
    .Read_Resistor_2(Rt), .CLK(Clock_out), .CLK_2(Reg_CLR_out));
  assign bit_extender_2_out = {{27{1'b0}}, Rd};  // Bit_Extender bit_extender_2
  Adder #(.width(16)) adder_1 (.a(16'h1), .b(register_1_q), .out(adder_1_out));  // open: cin, cout
  assign bit_extender_3_out = {{17{1'b0}}, {Rs, Rt, Rd}};  // Bit_Extender bit_extender_3
  assign bit_extender_4_out = {{16{1'b0}}, adder_1_out};  // Bit_Extender bit_extender_4
  Multiplexer #(.width(32), .enable("false")) multiplexer_2 (
    .in0(n32_bit_register_1_read_data_2), .in1(bit_extender_2_out), .out(out_3), .sel(control_unit_1_alu_src));
  Bit_Extender #(.in_width(32), .out_width(19)) bit_extender_5 (
    .in(n32_bit_register_1_read_data_2), .out(bit_extender_5_out));
  Adder #(.width(32)) adder_2 (.a(bit_extender_4_out), .b(bit_extender_2_out), .out(adder_2_out));  // open: cin, cout
  Multiplexer #(.width(32), .enable("false")) multiplexer_3 (
    .in0(bit_extender_4_out), .in1(adder_2_out), .out(multiplexer_3_out), .sel(and_1_out));
  _32_Bit_ALU u_32_bit_alu_1 (
    .Result(out_1), .Cout(out_8), .Zero(n32_bit_alu_1_zero), .A(out_4), .B(out_3), .Cin(control_unit_1_c_in),
    .Binv(control_unit_1_b_inv), .ALU_op(Alu_op));
  and and_1 (and_1_out, n32_bit_alu_1_zero, control_unit_1_branch);
  Multiplexer #(.width(32), .enable("false")) multiplexer_4 (
    .in0(multiplexer_3_out), .in1(bit_extender_3_out), .out(multiplexer_4_out), .sel(control_unit_1_jump));
  Bit_Extender #(.in_width(32), .out_width(24)) bit_extender_6 (.in(out_1), .out(bit_extender_6_out));
  RAM #(.addrWidth(24), .dataWidth(19), .bus("separate")) ram_1 (
    .addr(bit_extender_6_out), .din(bit_extender_5_out), .data(ram_1_data), .str(control_unit_1_str),
    .sel(control_unit_1_memsel), .clk(Clock_out), .ld(control_unit_1_ld), .clr(RAM_CLR_out));
  Button RAM_CLR (.out(RAM_CLR_out));
  assign bit_extender_7_out = {{13{1'b0}}, ram_1_data};  // Bit_Extender bit_extender_7
  Multiplexer #(.width(32), .enable("false")) multiplexer_5 (
    .in0(out_1), .in1(bit_extender_7_out), .out(out_2), .sel(control_unit_1_mem2reg));
endmodule

module Control_Unit (
  input  [3:0] in_1,
  output [4:0] ALU_Op,
  output Write_Register,
  output B_inv,
  output C_in,
  output RegDest,
  output Alu_Src,
  output Mem2Reg,
  output Str,
  output Ld,
  output MemSel,
  output Branch,
  output Jump
);

  wire decoder_1_out0, decoder_1_out5, decoder_1_out6, decoder_1_out7, decoder_1_out9, decoder_1_out10;

  Decoder #(.select(4), .enable("false")) decoder_1 (
    .out0(decoder_1_out0), .out1(Ld), .out2(Branch), .out3(B_inv), .out4(Jump), .out5(decoder_1_out5),
    .out6(decoder_1_out6), .out7(decoder_1_out7), .out8(Str), .out9(decoder_1_out9), .out10(decoder_1_out10),
    .sel(in_1));  // open: out11, out12, out13, out14, out15
  or or_1 (MemSel, Ld, Str);
  or or_2 (ALU_Op[4], Jump, Branch);
  or or_3 (ALU_Op[3], Jump, Branch);
  or or_4 (ALU_Op[2], Branch, Jump, decoder_1_out7);
  or or_5 (ALU_Op[1], decoder_1_out6, decoder_1_out5, Jump, Branch);
  or or_6 (ALU_Op[0], decoder_1_out10, decoder_1_out9, Str, decoder_1_out6, Jump, B_inv, Branch, Ld);
  or or_7 (Write_Register, decoder_1_out10, decoder_1_out9, decoder_1_out7, decoder_1_out6, decoder_1_out5, B_inv, Ld);
  or or_8 (RegDest, Ld, decoder_1_out9);
  or or_9 (Alu_Src, Ld, Str, decoder_1_out9);

  assign C_in = B_inv;
  assign Mem2Reg = Ld;
endmodule
